// Logisim project bcd.circ as structural Verilog: 1 circuit, main circuit implementation
module implementation (
  input  w3,
  input  w2,
  input  w1,
  input  w0,
  output a,
  output b,
  output c,
  output d,
  output e,
  output f,
  output g
);

  wire and_1_out, and_2_out, and_3_out, and_4_out, and_5_out, and_6_out, and_7_out, and_8_out, and_9_out,
       and_10_out, and_11_out, and_12_out, and_13_out, and_14_out, and_15_out, and_16_out, and_17_out,
       and_18_out, and_19_out, not_1_out, not_2_out, not_3_out, not_4_out, not_5_out, not_6_out, not_7_out,
       not_8_out, not_9_out, not_10_out, not_11_out, not_12_out, not_13_out, not_14_out, not_15_out,
       not_16_out, not_17_out, not_18_out, not_19_out, not_20_out, not_21_out, not_22_out, not_23_out,
       not_24_out, not_25_out, not_26_out, not_27_out, not_28_out, not_29_out;

  not not_1 (not_1_out, w2);
  not not_2 (not_2_out, w1);
  not not_3 (not_3_out, w0);
  not not_4 (not_4_out, w1);
  not not_5 (not_5_out, w3);
  not not_6 (not_6_out, w2);
  not not_7 (not_7_out, w1);
  not not_8 (not_8_out, w0);
  not not_9 (not_9_out, w3);
  not not_10 (not_10_out, w0);
  not not_11 (not_11_out, w1);
  not not_12 (not_12_out, w3);
  not not_13 (not_13_out, w2);
  not not_14 (not_14_out, w0);
  and and_1 (and_1_out, w2, w0);
  and and_2 (and_2_out, not_1_out, not_2_out, not_3_out);
  and and_3 (and_3_out, not_6_out, not_7_out, not_8_out);
  and and_4 (and_4_out, not_9_out, w1, not_10_out);
  and and_5 (and_5_out, w2, not_11_out);
  and and_6 (and_6_out, not_12_out, not_13_out, w1);
  and and_7 (and_7_out, w1, not_14_out);
  and and_8 (and_8_out, not_5_out, w2);
  and and_9 (and_9_out, w1, w0);
  or or_1 (e, and_3_out, and_4_out);
  or or_2 (c, not_4_out, w3, and_8_out, and_9_out);
  or or_3 (g, w3, and_5_out, and_6_out, and_7_out);
  or or_4 (a, w3, and_1_out, and_2_out, w1);
  not not_15 (not_15_out, w3);
  not not_16 (not_16_out, w2);
  not not_17 (not_17_out, w1);
  not not_18 (not_18_out, w0);
  not not_19 (not_19_out, w2);
  not not_20 (not_20_out, w1);
  not not_21 (not_21_out, w0);
  not not_22 (not_22_out, w1);
  not not_23 (not_23_out, w1);
  not not_24 (not_24_out, w0);
  not not_25 (not_25_out, w1);
  not not_26 (not_26_out, w0);
  and and_10 (and_10_out, not_15_out, not_16_out);
  and and_11 (and_11_out, w1, w0);
  and and_12 (and_12_out, not_17_out, not_18_out);
  not not_27 (not_27_out, w3);
  not not_28 (not_28_out, w2);
  not not_29 (not_29_out, w0);
  and and_13 (and_13_out, not_19_out, not_20_out, not_21_out);
  and and_14 (and_14_out, w2, not_22_out, w0);
  and and_15 (and_15_out, not_27_out, not_28_out, w1);
  and and_16 (and_16_out, w1, not_29_out);
  and and_17 (and_17_out, not_23_out, not_24_out);
  and and_18 (and_18_out, w2, not_25_out);
  and and_19 (and_19_out, w2, w1, not_26_out);
  or or_5 (b, and_10_out, and_11_out, and_12_out, w3);
  or or_6 (f, w3, and_17_out, and_18_out, and_19_out);
  or or_7 (d, and_13_out, w3, and_14_out, and_15_out, and_16_out);

  // Other names for the same wires on the sheet: at = a; bt = b; ct = c; dt = d; et = e; ft = f; gt = g; w0t = w0;
  //   w1t = w1; w2t = w2; w3t = w3
endmodule
